// Digital circuit display.dig as structural Verilog
module display (
  input  clock,
  input  enable,
  input  [15:0] Character_Data,
  output [3:0] R,
  output [3:0] G,
  output [3:0] B,
  output H_output,
  output V_output,
  output [10:0] Character_Address
);

  wire sync_1_horizontal, sync_1_picture, sync_1_vertical;
  wire [3:0] character_position_1_p4;
  wire [4:0] character_position_1_p3;
  wire [6:0] strings_1_character_o;
  wire [7:0] character_position_1_p5, character_position_1_p6;
  wire [11:0] strings_1_background_o, strings_1_foreground_o;
  wire [15:0] sync_1_x, sync_1_y;

  sync sync_1 (
    .clock(clock), .Horizontal(sync_1_horizontal), .Vertical(sync_1_vertical), .picture(sync_1_picture),
    .X(sync_1_x), .Y(sync_1_y));
  // character_position character_position_1: pin names not known; wires that end beside it: sync_1_x, sync_1_y, character_position_1_p3, character_position_1_p4, character_position_1_p5, character_position_1_p6
  strings strings_1 (
    .CX(character_position_1_p5), .CY(character_position_1_p6), .foreground(12'h9e), .background(12'h1),
    .character({7{1'b0}}), .foreground__colour(12'h3c1), .background__colour(12'h1), .CX__colour(4'b0010),
    .CY_colour({8{1'b0}}), .Character_0(7'b0111000), .Character_1(7'b0101101), .Character_2(7'b1000010),
    .Character_3(7'b1010101), .Character_4(7'b1010100), .Character_5(7'b0100000), .Character_6(7'b1001101),
    .Character_7(7'b1001001), .Character_8(7'b1000111), .Character_9(7'b1001000), .Character_10(7'b1010100),
    .Character_11(7'b1011001), .Character_12(7'b0100000), .Character_13(7'b1010110),
    .Character_14(7'b1000111), .Character_15(7'b1000001), .enable(enable),
    .character_o(strings_1_character_o), .foreground_o(strings_1_foreground_o),
    .background_o(strings_1_background_o));  // open: CX_o, CY_o
  text text_1 (
    .H_input(sync_1_horizontal), .V_input(sync_1_vertical), .picture(sync_1_picture),
    .row(character_position_1_p3), .column(character_position_1_p4), .clock(clock),
    .character(strings_1_character_o), .foreground(strings_1_foreground_o),
    .background(strings_1_background_o), .Character_Data(Character_Data), .R(R), .G(G), .B(B),
    .H_output(H_output), .V_output(V_output), .Character_Address(Character_Address));

  // Other names for the same wires on the sheet: C = clock

  // Notes on the sheet:
  //   clock: Hz: 2147483647
endmodule
